# Fritzing sketch Rotary Encoder - GC9A01 (saved by Fritzing 0.9.10b)

parts:
  Part1 = Arduino Nano (Rev3.0)
  RE1 = KY-040 Rotary encoder [package=THT]
  Part3 = Arduino Mega 2560 (Rev3)

nets:
  GND: Part1.GND, RE1.GND, Part3.GND
  N1: Part1.D2, RE1.SW
  N2: Part1.D5, RE1.DT
  N3: Part1.D6, RE1.CLK
  5V: Part1.5V, RE1.Vcc
  N4: Part1.A5, Part3.D21/SCL
  N5: Part1.A4, Part3.D20/SDA

custom parts:
  KY-040 Rotary encoder: KY-040 Rotary Encoder with switch on breakout borad from AZ Delivery
