# Fritzing sketch Rotary Encoder (saved by Fritzing 0.9.10b)

parts:
  Part1 = Arduino Nano (Rev3.0)
  Part2 = OLED Monochrome 128x64 1.3 inch [part_number=938]
  RE1 = KY-040 Rotary encoder [package=THT]
  Part3 = Arduino Mega 2560 (Rev3)

nets:
  N1: Part1.RESET, Part2.RESET
  GND: Part1.GND, Part2.GND, RE1.GND, Part3.GND
  N2: Part1.D2, RE1.SW
  N3: Part1.D5, RE1.DT
  N4: Part1.D6, RE1.CLK
  N5: Part1.D7, Part2.CS
  N6: Part1.D9, Part2.DC_SA0
  N7: Part1.D11/MOSI, Part2.MOSI_SDA
  5V: Part1.5V, Part2.VIN, RE1.Vcc
  N8: Part1.A5, Part3.D21/SCL
  N9: Part1.A4, Part3.D20/SDA
  N10: Part1.D13/SCK, Part2.SCLK_SCK

custom parts:
  OLED Monochrome 128x64 1.3 inch: These displays are small, only about 1.3" diagonal, but very readable due to the high contrast of an OLED display. This display is made of 128x64 individual white OLED pixels, each one is turned on or off by the controller chip. Because the display makes its own light, no backlight is required. This reduces the power required to run the OLED and is why the display has such high contrast; we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
  KY-040 Rotary encoder: KY-040 Rotary Encoder with switch on breakout borad from AZ Delivery
