# Fritzing sketch Serial Throttle - I2C OLED (saved by Fritzing 0.9.10b)

parts:
  Part1 = Arduino Nano (Rev3.0)
  U1 = SLIDER [knob_status=50% power=0.5W package=slider]
  U2 = SLIDER [knob_status=50% power=0.5W package=slider]
  U3 = SLIDER [knob_status=50% power=0.5W package=slider]
  KEYPAD1 = Membrane Matrix Keypad
  o1 = Module display OLED I2C 128x64 SSD1306 [package=THT]

nets:
  N1: Part1.D2, KEYPAD1.1
  N2: Part1.D3, KEYPAD1.2
  N3: Part1.D4, KEYPAD1.3
  N4: Part1.D5, KEYPAD1.4
  N5: Part1.D6, KEYPAD1.5
  N6: Part1.D7, KEYPAD1.6
  N7: Part1.D8, KEYPAD1.7
  GND: Part1.GND, U1.E, U2.E, U3.E, o1.GND
  5V: Part1.5V, U1.A, U2.A, U3.A, o1.VCC
  N8: Part1.A5, o1.SCL
  N9: Part1.A4, o1.SDA
  N10: Part1.A2, U1.S
  N11: Part1.A1, U2.S
  N12: Part1.A0, U3.S

custom parts:
  Membrane Matrix Keypad: Membrane Matrix 3x4 Keypad
  Module display OLED I2C 128x64 SSD1306: Ecran OLED I2C SSD163 de 128x64 avec connexion I2C
