# Fritzing sketch Serial Throttle (saved by Fritzing 0.9.10b)

parts:
  Part1 = Arduino Nano (Rev3.0)
  U1 = SLIDER [knob_status=50% power=0.5W package=slider]
  U2 = SLIDER [knob_status=50% power=0.5W package=slider]
  U3 = SLIDER [knob_status=50% power=0.5W package=slider]
  Part3 = OLED Monochrome 128x64 1.3 inch [part_number=938]
  KEYPAD1 = Membrane Matrix Keypad

nets:
  N1: Part1.RESET, Part3.RESET
  N2: Part1.D2, KEYPAD1.1
  N3: Part1.D3, KEYPAD1.2
  N4: Part1.D4, KEYPAD1.3
  N5: Part1.D5, KEYPAD1.4
  N6: Part1.D6, KEYPAD1.5
  N7: Part1.D7, KEYPAD1.6
  N8: Part1.D8, KEYPAD1.7
  N9: Part1.D9, Part3.DC_SA0
  N10: Part1.D10, Part3.CS
  N11: Part1.D11/MOSI, Part3.MOSI_SDA
  GND: Part1.GND, U1.E, U2.E, U3.E, Part3.GND
  5V: Part1.5V, U1.A, U2.A, U3.A, Part3.VIN
  N12: Part1.A2, U1.S
  N13: Part1.A1, U2.S
  N14: Part1.A0, U3.S
  N15: Part1.D13/SCK, Part3.SCLK_SCK

custom parts:
  OLED Monochrome 128x64 1.3 inch: These displays are small, only about 1.3" diagonal, but very readable due to the high contrast of an OLED display. This display is made of 128x64 individual white OLED pixels, each one is turned on or off by the controller chip. Because the display makes its own light, no backlight is required. This reduces the power required to run the OLED and is why the display has such high contrast; we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
  Membrane Matrix Keypad: Membrane Matrix 3x4 Keypad
